// Logisim project Circuit Sortie G.circ as structural Verilog: 5 circuits, main circuit main
module main (
  input  D,
  input  T,
  input  C,
  input  B,
  input  G,
  input  P,
  output out_7
);

  wire n1_1_out_4, n2_1_out_6, n3_1_out_5, n4_1_out_5;

  _1 u_1_1 (.D(D), .B(B), .G(G), .out_4(n1_1_out_4));
  _2 u_2_1 (.D(D), .T(T), .C(C), .B(B), .G(G), .out_6(n2_1_out_6));
  _3 u_3_1 (.D(D), .B(B), .G(G), .P(P), .out_5(n3_1_out_5));
  _4 u_4_1 (.D(D), .T(T), .B(B), .G(G), .out_5(n4_1_out_5));
  or or_1 (out_7, n1_1_out_4, n2_1_out_6, n3_1_out_5, n4_1_out_5);

  // Notes on the sheet:
  //   Sortie G, Sofiane AIBIBAOUEN
endmodule

module _1 (
  input  D,
  input  B,
  input  G,
  output out_4
);

  and and_1 (out_4, D, ~B, G);  // AND_Gate
endmodule

module _2 (
  input  D,
  input  T,
  input  C,
  input  B,
  input  G,
  output out_6
);

  and and_1 (out_6, D, ~T, ~C, B, G);  // AND_Gate
endmodule

module _3 (
  input  D,
  input  B,
  input  G,
  input  P,
  output out_5
);

  and and_1 (out_5, D, B, G, ~P);  // AND_Gate
endmodule

module _4 (
  input  D,
  input  T,
  input  B,
  input  G,
  output out_5
);

  and and_1 (out_5, D, T, B, G);
endmodule
