// Logisim project Circuit Sortie P.circ as structural Verilog: 5 circuits, main circuit Sortie P
module Sortie_P (
  input  D,
  input  T,
  input  C,
  input  B,
  input  G,
  input  P,
  output out_7
);

  wire n1_1_out_6, n2_1_out_5, n4_1_out_7;

  _1 u_1_1 (.D(D), .T(T), .B(B), .G(G), .P(P), .out_6(n1_1_out_6));
  _2 u_2_1 (.D(D), .B(B), .G(G), .P(P), .out_5(n2_1_out_5));
  _4 u_4_1 (.D(D), .T(T), .C(C), .B(B), .G(G), .P(P), .out_7(n4_1_out_7));
  or or_1 (out_7, n1_1_out_6, n2_1_out_5, n4_1_out_7);

  // Notes on the sheet:
  //   Sortie P, Sofiane AIBIBAOUEN
endmodule

module _1 (
  input  D,
  input  T,
  input  B,
  input  G,
  input  P,
  output out_6
);

  wire not_1_out, not_2_out;

  not not_1 (not_1_out, B);
  not not_2 (not_2_out, G);
  and and_1 (out_6, D, T, not_1_out, not_2_out, P);
endmodule

module _2 (
  input  D,
  input  B,
  input  G,
  input  P,
  output out_5
);

  and and_1 (out_5, D, B, ~G, P);  // AND_Gate
endmodule

module _3 (
  input  D,
  input  B,
  input  G,
  input  P,
  output out_5
);

  and and_1 (out_5, D, B, ~G, P);  // AND_Gate
endmodule

module _4 (
  input  D,
  input  T,
  input  C,
  input  B,
  input  G,
  input  P,
  output out_7
);

  and and_1 (out_7, D, ~T, C, B, G, P);  // AND_Gate
endmodule
