// Logisim project Circuite simplifié - Sofiane (118) AIBIBAOUEN.circ as structural Verilog: 1 circuit, main circuit main
module main (
  input  j,
  input  c,
  input  t,
  output S
);

  wire not_1_out;

  not not_1 (not_1_out, t);
  and and_1 (S, j, c, not_1_out);
endmodule
