// Logisim project Machine Projet NSI - Ismail Benkirane _ Sofiane Aibibaouen.circ as structural Verilog: 30 circuits, main circuit main
module main (
  input  D,
  input  T,
  input  C,
  input  B,
  input  G,
  input  P,
  output t_2,
  output c_2,
  output b_2,
  output p_2,
  output g_2,
  output e
);

  T t_1 (.d(D), .p(T), .g(C), .b(B), .c(G), .t(P), .out_7(t_2));
  C c_1 (.d(D), .p(T), .g(C), .b(B), .c(G), .t(P), .out_7(c_2));
  B b_1 (.d(D), .p(T), .g(C), .b(B), .c(G), .t(P), .out_7(b_2));
  P p_1 (.D(D), .T(T), .C(P), .B(C), .G(B), .P(G), .out_7(p_2));
  G g_1 (.D(D), .T(T), .C(C), .B(B), .G(G), .P(P), .out_7(g_2));
  E e_1 (.D(D), .T(T), .B(B), .G(G), .P(P), .out_6(e));
endmodule

module T (
  input  d,
  input  p,
  input  g,
  input  b,
  input  c,
  input  t,
  output out_7
);

  wire n1_1_out_5, n2_1_out_5, n3_1_out_6, n4_1_out_6;

  _1 u_1_1 (.d(d), .p(p), .b(b), .t(t), .out_5(n1_1_out_5));
  _3 u_3_1 (.d(d), .p(p), .b(b), .t(t), .c(c), .out_6(n3_1_out_6));
  _2 u_2_1 (.d(d), .g(g), .b(b), .t(t), .out_5(n2_1_out_5));
  _4 u_4_1 (.d(d), .g(g), .b(b), .t(t), .c(c), .out_6(n4_1_out_6));
  or or_1 (out_7, n1_1_out_5, n3_1_out_6, n2_1_out_5, n4_1_out_6);
endmodule

module _1 (
  input  d,
  input  p,
  input  b,
  input  t,
  output out_5
);

  wire not_1_out;

  not not_1 (not_1_out, b);
  and and_1 (out_5, d, p, not_1_out, t);
endmodule

module _2 (
  input  d,
  input  g,
  input  b,
  input  t,
  output out_5
);

  wire not_1_out;

  not not_1 (not_1_out, b);
  and and_1 (out_5, d, g, not_1_out, t);
endmodule

module _3 (
  input  d,
  input  p,
  input  b,
  input  t,
  input  c,
  output out_6
);

  and and_1 (out_6, d, p, b, t, c);
endmodule

module _4 (
  input  d,
  input  g,
  input  b,
  input  t,
  input  c,
  output out_6
);

  and and_1 (out_6, d, g, b, t, c);
endmodule

module C (
  input  d,
  input  p,
  input  g,
  input  b,
  input  c,
  input  t,
  output out_7
);

  wire n1_c_1_out_5, n2_c_1_out_5, n3_c_1_out_6, n4_c_1_out_6;

  _1_c u_1_c_1 (.d(d), .p(p), .b(b), .c(c), .out_5(n1_c_1_out_5));
  _3_c u_3_c_1 (.d(d), .p(p), .b(b), .t(t), .c(c), .out_6(n3_c_1_out_6));
  _2_c u_2_c_1 (.d(d), .g(g), .b(b), .c(c), .out_5(n2_c_1_out_5));
  _4_c u_4_c_1 (.d(d), .p(g), .b(b), .t(t), .c(c), .out_6(n4_c_1_out_6));
  or or_1 (out_7, n1_c_1_out_5, n3_c_1_out_6, n2_c_1_out_5, n4_c_1_out_6);
endmodule

module _1_c (
  input  d,
  input  p,
  input  b,
  input  c,
  output out_5
);

  wire not_1_out;

  not not_1 (not_1_out, b);
  and and_1 (out_5, d, p, not_1_out, c);
endmodule

module _2_c (
  input  d,
  input  g,
  input  b,
  input  c,
  output out_5
);

  wire not_1_out;

  not not_1 (not_1_out, b);
  and and_1 (out_5, d, g, not_1_out, c);
endmodule

module _3_c (
  input  d,
  input  p,
  input  b,
  input  t,
  input  c,
  output out_6
);

  wire not_1_out;

  not not_1 (not_1_out, t);
  and and_1 (out_6, d, p, b, not_1_out, c);
endmodule

module _4_c (
  input  d,
  input  p,
  input  b,
  input  t,
  input  c,
  output out_6
);

  wire not_1_out;

  not not_1 (not_1_out, t);
  and and_1 (out_6, d, p, b, not_1_out, c);
endmodule

module B (
  input  d,
  input  p,
  input  g,
  input  b,
  input  c,
  input  t,
  output out_7
);

  wire n1_b_1_out_5, n2_b_1_out_5, n3_b_1_out_5, n4_b_1_out_5;

  _1_b u_1_b_1 (.d(d), .p(p), .b(b), .t(t), .out_5(n1_b_1_out_5));
  _2_b u_2_b_1 (.d(d), .g(g), .b(b), .t(t), .out_5(n2_b_1_out_5));
  _3_b u_3_b_1 (.d(d), .g(g), .b(b), .c(c), .out_5(n3_b_1_out_5));
  _4_b u_4_b_1 (.d(d), .p(p), .b(b), .c(c), .out_5(n4_b_1_out_5));
  or or_1 (out_7, n1_b_1_out_5, n2_b_1_out_5, n3_b_1_out_5, n4_b_1_out_5);
endmodule

module _1_b (
  input  d,
  input  p,
  input  b,
  input  t,
  output out_5
);

  wire not_1_out;

  not not_1 (not_1_out, t);
  and and_1 (out_5, d, p, b, not_1_out);
endmodule

module _2_b (
  input  d,
  input  g,
  input  b,
  input  t,
  output out_5
);

  wire not_1_out;

  not not_1 (not_1_out, t);
  and and_1 (out_5, d, g, b, not_1_out);
endmodule

module _3_b (
  input  d,
  input  g,
  input  b,
  input  c,
  output out_5
);

  wire not_1_out;

  not not_1 (not_1_out, c);
  and and_1 (out_5, d, g, b, not_1_out);
endmodule

module _4_b (
  input  d,
  input  p,
  input  b,
  input  c,
  output out_5
);

  wire not_1_out;

  not not_1 (not_1_out, c);
  and and_1 (out_5, d, p, b, not_1_out);
endmodule

module P (
  input  D,
  input  T,
  input  C,
  input  B,
  input  G,
  input  P,
  output out_7
);

  wire n1_p_1_out_6, n2_p_1_out_5, n2_p_2_out_5, n4_p_1_out_7;

  _1_p u_1_p_1 (.D(D), .T(T), .B(B), .G(G), .P(P), .out_6(n1_p_1_out_6));
  _2_p u_2_p_1 (.D(D), .B(B), .G(G), .P(P), .out_5(n2_p_1_out_5));
  _4_p u_4_p_1 (.D(D), .T(T), .C(C), .B(B), .G(G), .P(P), .out_7(n4_p_1_out_7));
  _2_p u_2_p_2 (.D(D), .B(T), .G(P), .P(G), .out_5(n2_p_2_out_5));
  or or_1 (out_7, n1_p_1_out_6, n2_p_1_out_5, n2_p_2_out_5, n4_p_1_out_7);
endmodule

module _1_p (
  input  D,
  input  T,
  input  B,
  input  G,
  input  P,
  output out_6
);

  wire not_1_out, not_2_out;

  not not_1 (not_1_out, B);
  not not_2 (not_2_out, G);
  and and_1 (out_6, D, T, not_1_out, not_2_out, P);
endmodule

module _2_p (
  input  D,
  input  B,
  input  G,
  input  P,
  output out_5
);

  and and_1 (out_5, D, B, ~G, P);  // AND_Gate
endmodule

module _3_p (
  input  D,
  input  B,
  input  G,
  input  P,
  output out_5
);

  and and_1 (out_5, D, B, ~G, P);  // AND_Gate
endmodule

module _4_p (
  input  D,
  input  T,
  input  C,
  input  B,
  input  G,
  input  P,
  output out_7
);

  and and_1 (out_7, D, ~T, C, B, G, P);  // AND_Gate
endmodule

module G (
  input  D,
  input  T,
  input  C,
  input  B,
  input  G,
  input  P,
  output out_7
);

  wire n1_g_1_out_4, n2_g_1_out_6, n3_g_1_out_5, n4_g_1_out_5;

  _1_g u_1_g_1 (.D(D), .B(B), .G(G), .out_4(n1_g_1_out_4));
  _2_g u_2_g_1 (.D(D), .T(T), .C(C), .B(B), .G(G), .out_6(n2_g_1_out_6));
  _3_g u_3_g_1 (.D(D), .B(B), .G(G), .P(P), .out_5(n3_g_1_out_5));
  _4_g u_4_g_1 (.D(D), .T(T), .B(B), .G(G), .out_5(n4_g_1_out_5));
  or or_1 (out_7, n1_g_1_out_4, n2_g_1_out_6, n3_g_1_out_5, n4_g_1_out_5);
endmodule

module _1_g (
  input  D,
  input  B,
  input  G,
  output out_4
);

  and and_1 (out_4, D, ~B, G);  // AND_Gate
endmodule

module _2_g (
  input  D,
  input  T,
  input  C,
  input  B,
  input  G,
  output out_6
);

  and and_1 (out_6, D, ~T, ~C, B, G);  // AND_Gate
endmodule

module _3_g (
  input  D,
  input  B,
  input  G,
  input  P,
  output out_5
);

  and and_1 (out_5, D, B, G, ~P);  // AND_Gate
endmodule

module _4_g (
  input  D,
  input  T,
  input  B,
  input  G,
  output out_5
);

  and and_1 (out_5, D, T, B, G);
endmodule

module E (
  input  D,
  input  T,
  input  B,
  input  G,
  input  P,
  output out_6
);

  wire n1_e_1_out_5, n2_e_1_out_6, n3_e_1_out_5;

  _1_e u_1_e_1 (.D(D), .B(T), .G(B), .P(G), .out_5(n1_e_1_out_5));
  _2_e u_2_e_1 (.D(D), .T(T), .B(B), .G(G), .P(P), .out_6(n2_e_1_out_6));
  _3_e u_3_e_1 (.D(D), .B(B), .G(G), .P(P), .out_5(n3_e_1_out_5));
  or or_1 (out_6, n1_e_1_out_5, n2_e_1_out_6, n3_e_1_out_5);
endmodule

module _1_e (
  input  D,
  input  B,
  input  G,
  input  P,
  output out_5
);

  and and_1 (out_5, D, B, G, P);
endmodule

module _2_e (
  input  D,
  input  T,
  input  B,
  input  G,
  input  P,
  output out_6
);

  and and_1 (out_6, D, T, ~B, ~G, P);  // AND_Gate
endmodule

module _3_e (
  input  D,
  input  B,
  input  G,
  input  P,
  output out_5
);

  and and_1 (out_5, D, B, ~G, P);  // AND_Gate
endmodule
