// Logisim project Sortie B.circ as structural Verilog: 5 circuits, main circuit main
module dpbt (
  input  d,
  input  p,
  input  b,
  input  t,
  output out_5
);

  wire not_1_out;

  not not_1 (not_1_out, t);
  and and_1 (out_5, d, p, b, not_1_out);
endmodule

module dgb_t (
  input  d,
  input  g,
  input  b,
  input  t,
  output out_5
);

  wire not_1_out;

  not not_1 (not_1_out, t);
  and and_1 (out_5, d, g, b, not_1_out);
endmodule

module dgb_c (
  input  d,
  input  g,
  input  b,
  input  c,
  output out_5
);

  wire not_1_out;

  not not_1 (not_1_out, c);
  and and_1 (out_5, d, g, b, not_1_out);
endmodule

module dpb_c (
  input  d,
  input  p,
  input  b,
  input  c,
  output out_5
);

  wire not_1_out;

  not not_1 (not_1_out, c);
  and and_1 (out_5, d, p, b, not_1_out);
endmodule

module main (
  input  d,
  input  p,
  input  g,
  input  b,
  input  c,
  input  t,
  output out_7
);

  wire dgb_c_1_out_5, dgb_t_1_out_5, dpb_c_1_out_5, dpbt_1_out_5;

  dpbt dpbt_1 (.d(d), .p(p), .b(b), .t(t), .out_5(dpbt_1_out_5));
  dgb_t dgb_t_1 (.d(d), .g(g), .b(b), .t(t), .out_5(dgb_t_1_out_5));
  dgb_c dgb_c_1 (.d(d), .g(g), .b(b), .c(c), .out_5(dgb_c_1_out_5));
  dpb_c dpb_c_1 (.d(d), .p(p), .b(b), .c(c), .out_5(dpb_c_1_out_5));
  or or_1 (out_7, dpbt_1_out_5, dgb_t_1_out_5, dgb_c_1_out_5, dpb_c_1_out_5);

  // Notes on the sheet:
  //   Sortie B: Benkirane Ismaïl
endmodule
