// Logisim project Sortie C.circ as structural Verilog: 5 circuits, main circuit main
module main (
  input  d,
  input  p,
  input  g,
  input  b,
  input  c,
  input  t,
  output out_7
);

  wire dg_b_c_1_out_5, dgb_t_c_1_out_6, dp_b_c_1_out_5, dpb_t_c_1_out_6;

  dp_b__c dp_b_c_1 (.d(d), .p(p), .b(b), .c(c), .out_5(dp_b_c_1_out_5));
  dpb_t__c dpb_t_c_1 (.d(d), .p(p), .b(b), .t(t), .c(c), .out_6(dpb_t_c_1_out_6));
  dg_b__c dg_b_c_1 (.d(d), .g(g), .b(b), .c(c), .out_5(dg_b_c_1_out_5));
  dgb_t__c dgb_t_c_1 (.d(d), .p(g), .b(b), .t(t), .c(c), .out_6(dgb_t_c_1_out_6));
  or or_1 (out_7, dp_b_c_1_out_5, dpb_t_c_1_out_6, dg_b_c_1_out_5, dgb_t_c_1_out_6);

  // Notes on the sheet:
  //   Sortie C: Benkirane Ismaïl
endmodule

module dp_b__c (
  input  d,
  input  p,
  input  b,
  input  c,
  output out_5
);

  wire not_1_out;

  not not_1 (not_1_out, b);
  and and_1 (out_5, d, p, not_1_out, c);
endmodule

module dg_b__c (
  input  d,
  input  g,
  input  b,
  input  c,
  output out_5
);

  wire not_1_out;

  not not_1 (not_1_out, b);
  and and_1 (out_5, d, g, not_1_out, c);
endmodule

module dpb_t__c (
  input  d,
  input  p,
  input  b,
  input  t,
  input  c,
  output out_6
);

  wire not_1_out;

  not not_1 (not_1_out, t);
  and and_1 (out_6, d, p, b, not_1_out, c);
endmodule

module dgb_t__c (
  input  d,
  input  p,
  input  b,
  input  t,
  input  c,
  output out_6
);

  wire not_1_out;

  not not_1 (not_1_out, t);
  and and_1 (out_6, d, p, b, not_1_out, c);
endmodule
