// Logisim project Sortie T.circ as structural Verilog: 5 circuits, main circuit main
module main (
  input  d,
  input  p,
  input  g,
  input  b,
  input  c,
  input  t,
  output out_7
);

  wire dg_b_t_1_out_5, dgbtc_1_out_6, dp_b_t_1_out_5, dpbtc_1_out_6;

  dp_b__t dp_b_t_1 (.d(d), .p(p), .b(b), .t(t), .out_5(dp_b_t_1_out_5));
  dpbtc dpbtc_1 (.d(d), .p(p), .b(b), .t(t), .c(c), .out_6(dpbtc_1_out_6));
  dg_b__t dg_b_t_1 (.d(d), .g(g), .b(b), .t(t), .out_5(dg_b_t_1_out_5));
  dgbtc dgbtc_1 (.d(d), .g(g), .b(b), .t(t), .c(c), .out_6(dgbtc_1_out_6));
  or or_1 (out_7, dp_b_t_1_out_5, dpbtc_1_out_6, dg_b_t_1_out_5, dgbtc_1_out_6);

  // Notes on the sheet:
  //   Sortie T: Benkirane Ismaïl
endmodule

module dp_b__t (
  input  d,
  input  p,
  input  b,
  input  t,
  output out_5
);

  wire not_1_out;

  not not_1 (not_1_out, b);
  and and_1 (out_5, d, p, not_1_out, t);
endmodule

module dg_b__t (
  input  d,
  input  g,
  input  b,
  input  t,
  output out_5
);

  wire not_1_out;

  not not_1 (not_1_out, b);
  and and_1 (out_5, d, g, not_1_out, t);
endmodule

module dpbtc (
  input  d,
  input  p,
  input  b,
  input  t,
  input  c,
  output out_6
);

  and and_1 (out_6, d, p, b, t, c);
endmodule

module dgbtc (
  input  d,
  input  g,
  input  b,
  input  t,
  input  c,
  output out_6
);

  and and_1 (out_6, d, g, b, t, c);
endmodule
