// Logisim project Sous-circuit (4.3) - Sofiane (118) AIBIBAOUEN.circ as structural Verilog: 2 circuits, main circuit main
module main (
  input  in_1,
  input  in_2,
  input  in_3,
  output out_4
);

  Sous_circuit_4_2 sous_circuit_4_2_1 (.in_1(in_1), .in_2(in_2), .in_3(in_3), .out_4(out_4));
endmodule

module Sous_circuit_4_2 (
  input  in_1,
  input  in_2,
  input  in_3,
  output out_4
);

  wire not_1_out;

  not not_1 (not_1_out, in_3);
  and and_1 (out_4, in_1, in_2, not_1_out);
endmodule
