// Logisim project Sous-circuit (4.4) - Sofiane (118) AIBIBAOUEN.circ as structural Verilog
module main (
  input  j,
  input  c,
  input  t,
  input  l,
  output out_5
);

  Sous_circuit__t sous_circuit_t_1 (.in_1(l), .in_2(j), .in_3(j), .out_4(out_5));
  Sous_circuit_4_2 sous_circuit_4_2_1 (.j(j), .c(c), .t(j), .out_4(out_5));
  Sous_circuit__t sous_circuit_t_2 (.in_1(j), .in_2(j), .in_3(l), .out_4(out_5));
  Sous_circuit__l sous_circuit_l_1 (.j(j), .c(c), .l(j), .t(l), .out_5(out_5));

  assign t = j;
endmodule

module Sous_circuit_4_2 (
  input  j,
  input  c,
  input  t,
  output out_4
);

  wire not_1_out;

  not not_1 (not_1_out, t);
  and and_1 (out_4, j, c, not_1_out);
endmodule

module Sous_circuit__t (
  input  in_1,
  input  in_2,
  input  in_3,
  output out_4
);

  and and_1 (out_4, in_1, in_2, in_2, in_2);
  and and_2 (out_4, in_1, in_2, in_3, in_3);
endmodule

module Sous_circuit__l (
  input  j,
  input  c,
  input  l,
  input  t,
  output out_5
);

  wire and_1_out, and_2_out, and_3_out;

  and and_1 (and_1_out, j, l, c);
  and and_2 (and_2_out, j, l);
  and and_3 (and_3_out, j, l, t);
  or or_1 (out_5, and_2_out, and_1_out, and_3_out);
endmodule

module XOR (
  input  in_1,
  input  in_2,
  output out_3
);

  wire and_1_out, and_2_out, not_1_out, not_2_out;

  not not_1 (not_1_out, in_2);
  not not_2 (not_2_out, in_1);
  and and_1 (and_1_out, in_1, in_1, not_1_out);
  and and_2 (and_2_out, not_2_out, in_2);
  or or_1 (out_3, and_1_out, and_2_out);
endmodule
